// Logisim project logisim_sCPU.circ as structural Verilog: 10 circuits, main circuit main
module main (
  input  rst,
  input  clk,
  output [3:0] out_3
);

  wire bin_seg_1_b, bin_seg_1_c, bin_seg_1_e, bin_seg_1_f, bin_seg_1_g, bin_seg_1_out_8, bin_seg_1_out_11,
       bin_seg_2_b, bin_seg_2_c, bin_seg_2_e, bin_seg_2_f, bin_seg_2_g, bin_seg_2_out_8, bin_seg_2_out_11,
       or_1_out, scpu_1_1_is_add, scpu_1_1_is_bner0, scpu_1_1_is_li, scpu_1_1_is_out;
  wire [1:0] multiplexer_2_out, scpu_1_1_rd, scpu_1_1_rs1, scpu_1_1_rs2;
  wire [3:0] multiplexer_1_out, pc_next_1_pc_n, scpu_1_1_addr, scpu_1_1_imm;
  wire [7:0] adder_1_out, gpr_1_read1_out, gpr_1_read2_out, register_1_q, write_data_1_w_data;

  Multiplexer #(.width(4)) multiplexer_1 (.in0(pc_next_1_pc_n), .in1(4'b0000), .out(multiplexer_1_out), .sel(rst));
  sCPU_1 scpu_1_1 (
    .pc_in(multiplexer_1_out), .we(1'b1), .clk(clk), .imm(scpu_1_1_imm), .rs2(scpu_1_1_rs2),
    .rs1(scpu_1_1_rs1), .rd(scpu_1_1_rd), .is_add(scpu_1_1_is_add), .is_li(scpu_1_1_is_li),
    .addr(scpu_1_1_addr), .is_bner0(scpu_1_1_is_bner0), .is_out(scpu_1_1_is_out), .pc_out(out_3));  // open: opcode
  Multiplexer #(.width(2)) multiplexer_2 (
    .in0(scpu_1_1_rs1), .in1(2'b00), .out(multiplexer_2_out), .sel(scpu_1_1_is_bner0));
  or or_1 (or_1_out, scpu_1_1_is_add, scpu_1_1_is_li);
  gpr gpr_1 (
    .we(or_1_out), .write_addr(scpu_1_1_rd), .clk(clk), .read_addr1(multiplexer_2_out),
    .write_data(write_data_1_w_data), .read_addr2(scpu_1_1_rs2), .read2_out(gpr_1_read2_out),
    .read1_out(gpr_1_read1_out));
  Register register_1 (.D(gpr_1_read2_out), .en(scpu_1_1_is_out), .clk(clk), .Q(register_1_q));  // open: clr
  Adder adder_1 (.a(gpr_1_read2_out), .b(gpr_1_read1_out), .out(adder_1_out));  // open: cin, cout
  write_data write_data_1 (
    .imm(scpu_1_1_imm), .alu_out(adder_1_out), .is_li(scpu_1_1_is_li), .is_add(scpu_1_1_is_add),
    .w_data(write_data_1_w_data));
  pc_next pc_next_1 (
    .pc(out_3), .addr(scpu_1_1_addr), .r_data1(gpr_1_read1_out), .r_data2(gpr_1_read2_out),
    .is_bner0(scpu_1_1_is_bner0), .pc_n(pc_next_1_pc_n));
  bin_seg bin_seg_1 (
    .D(register_1_q[7]), .in_2(register_1_q[6]), .in_3(register_1_q[5]), .A(register_1_q[4]),
    .g(bin_seg_1_g), .f(bin_seg_1_f), .e(bin_seg_1_e), .out_8(bin_seg_1_out_8), .c(bin_seg_1_c),
    .b(bin_seg_1_b), .out_11(bin_seg_1_out_11));
  bin_seg bin_seg_2 (
    .D(register_1_q[3]), .in_2(register_1_q[2]), .in_3(register_1_q[1]), .A(register_1_q[0]),
    .g(bin_seg_2_g), .f(bin_seg_2_f), .e(bin_seg_2_e), .out_8(bin_seg_2_out_8), .c(bin_seg_2_c),
    .b(bin_seg_2_b), .out_11(bin_seg_2_out_11));
  _7_Segment_Display u_7_segment_display_1 (
    .g(bin_seg_1_out_11), .f(bin_seg_1_b), .a(bin_seg_1_g), .b(bin_seg_1_f), .e(bin_seg_1_c),
    .d(bin_seg_1_out_8), .c(bin_seg_1_e));  // open: dp
  _7_Segment_Display u_7_segment_display_2 (
    .g(bin_seg_2_out_11), .f(bin_seg_2_b), .a(bin_seg_2_g), .b(bin_seg_2_f), .e(bin_seg_2_c),
    .d(bin_seg_2_out_8), .c(bin_seg_2_e));  // open: dp
endmodule

module pc (
  input  [3:0] pc_in,
  input  WE,
  input  clk,
  output [3:0] pc_out
);

  Register #(.width(4)) pc (.D(pc_in), .en(WE), .clk(clk), .Q(pc_out));  // open: clr
endmodule

module decode (
  input  [31:0] instr,
  output lw,
  output lbu,
  output [4:0] rd,
  output addi,
  output [4:0] rs1,
  output [4:0] rs2,
  output sb,
  output sw,
  output [31:0] immU,
  output add,
  output [31:0] immI,
  output [31:0] immS,
  output lui,
  output jalr,
  output ebreak
);

  wire decoder_1_out3, decoder_1_out35, decoder_2_out2, decoder_2_out4, decoder_3_out0, decoder_3_out2;

  decode_imm decode_imm_1 (.instr(instr), .immU(immU), .immI(immI), .immS(immS));
  Decoder #(.select(7)) decoder_1 (
    .out3(decoder_1_out3), .out19(addi), .out35(decoder_1_out35), .out51(add), .out55(lui), .out103(jalr),
    .out115(ebreak), .sel(instr[6:0]), .en(1'b1));  // open: out0, out1, out2, out4, out5, out6, out7, out8, out9, out10, out11, out12, out13, out14, out15, out16, out17, out18, out20, out21, out22, out23, out24, out25, out26, out27, out28, out29, out30, out31, out32, out33, out34, out36, out37, out38, out39, out40, out41, out42, out43, out44, out45, out46, out47, out48, out49, out50, out52, out53, out54, out56, out57, out58, out59, out60, out61, out62, out63, out64, out65, out66, out67, out68, out69, out70, out71, out72, out73, out74, out75, out76, out77, out78, out79, out80, out81, out82, out83, out84, out85, out86, out87, out88, out89, out90, out91, out92, out93, out94, out95, out96, out97, out98, out99, out100, out101, out102, out104, out105, out106, out107, out108, out109, out110, out111, out112, out113, out114, out116, out117, out118, out119, out120, out121, out122, out123, out124, out125, out126, out127
  Decoder #(.select(3)) decoder_2 (
    .out2(decoder_2_out2), .out4(decoder_2_out4), .sel(instr[14:12]), .en(1'b1));  // open: out0, out1, out3, out5, out6, out7
  Decoder #(.select(3)) decoder_3 (
    .out0(decoder_3_out0), .out2(decoder_3_out2), .sel(instr[14:12]), .en(1'b1));  // open: out1, out3, out4, out5, out6, out7
  and and_1 (lw, decoder_1_out3, decoder_2_out2);
  and and_2 (lbu, decoder_2_out4, decoder_1_out3);
  and and_3 (sb, decoder_1_out35, decoder_3_out0);
  and and_4 (sw, decoder_3_out2, decoder_1_out35);

  assign rd = instr[11:7];
  assign rs1 = instr[19:15];
  assign rs2 = instr[24:20];

  // Other names for the same wires on the sheet: funct3[2:0] = instr[14:12]
endmodule

module sCPU_1 (
  input  [3:0] pc_in,
  input  we,
  input  clk,
  output [3:0] imm,
  output [1:0] rs2,
  output [1:0] rs1,
  output [1:0] rd,
  output is_add,
  output [1:0] opcode,
  output is_li,
  output [3:0] addr,
  output is_bner0,
  output is_out,
  output [3:0] pc_out
);

  wire [7:0] MEM_data;

  ROM #(.addrWidth(4)) MEM (.addr(pc_out), .data(MEM_data));
  pc pc_1 (.pc_in(pc_in), .WE(we), .clk(clk), .pc_out(pc_out));
  // decode decode_1: pin names not known; wires that end beside it: MEM_data[0], MEM_data[1], MEM_data[2], MEM_data[3], MEM_data[4], MEM_data[5], MEM_data[6], MEM_data[7], imm, rs2, rs1, rd, is_add, opcode, is_li, addr, is_bner0, is_out

  // Notes on the sheet:
  //   contents of MEM (hex, n*v repeats v):
  //   8a 90 a0 b1 17 29 42 d1 df
endmodule

module gpr (
  input  we,
  input  [1:0] write_addr,
  input  clk,
  input  [1:0] read_addr1,
  input  [7:0] write_data,
  input  [1:0] read_addr2,
  output [7:0] read2_out,
  output [7:0] read1_out
);

  gpr_unit gpr_unit_1 (
    .w_en(we), .w_addr(write_addr), .wd(write_data[0]), .clk(clk), .r1_addr(read_addr1),
    .r2_addr(read_addr2), .read2_out(read2_out[0]), .read1_out(read1_out[0]));
  gpr_unit gpr_unit_2 (
    .w_en(we), .w_addr(write_addr), .wd(write_data[1]), .clk(clk), .r1_addr(read_addr1),
    .r2_addr(read_addr2), .read2_out(read2_out[1]), .read1_out(read1_out[1]));
  gpr_unit gpr_unit_3 (
    .w_en(we), .w_addr(write_addr), .wd(write_data[2]), .clk(clk), .r1_addr(read_addr1),
    .r2_addr(read_addr2), .read2_out(read2_out[2]), .read1_out(read1_out[2]));
  gpr_unit gpr_unit_4 (
    .w_en(we), .w_addr(write_addr), .wd(write_data[3]), .clk(clk), .r1_addr(read_addr1),
    .r2_addr(read_addr2), .read2_out(read2_out[3]), .read1_out(read1_out[3]));
  gpr_unit gpr_unit_5 (
    .w_en(we), .w_addr(write_addr), .wd(write_data[4]), .clk(clk), .r1_addr(read_addr1),
    .r2_addr(read_addr2), .read2_out(read2_out[4]), .read1_out(read1_out[4]));
  gpr_unit gpr_unit_6 (
    .w_en(we), .w_addr(write_addr), .wd(write_data[5]), .clk(clk), .r1_addr(read_addr1),
    .r2_addr(read_addr2), .read2_out(read2_out[5]), .read1_out(read1_out[5]));
  gpr_unit gpr_unit_7 (
    .w_en(we), .w_addr(write_addr), .wd(write_data[6]), .clk(clk), .r1_addr(read_addr1),
    .r2_addr(read_addr2), .read2_out(read2_out[6]), .read1_out(read1_out[6]));
  gpr_unit gpr_unit_8 (
    .w_en(we), .w_addr(write_addr), .wd(write_data[7]), .clk(clk), .r1_addr(read_addr1),
    .r2_addr(read_addr2), .read2_out(read2_out[7]), .read1_out(read1_out[7]));
endmodule

module gpr_unit (
  input  w_en,
  input  [1:0] w_addr,
  input  wd,
  input  clk,
  input  [1:0] r1_addr,
  input  [1:0] r2_addr,
  output read2_out,
  output read1_out
);

  wire decoder_1_out0, decoder_1_out1, decoder_1_out2, decoder_1_out3, register_1_q, register_2_q,
       register_3_q, register_4_q;

  Decoder #(.select(2)) decoder_1 (
    .out0(decoder_1_out0), .out1(decoder_1_out1), .out2(decoder_1_out2), .out3(decoder_1_out3), .sel(w_addr),
    .en(w_en));
  Register #(.width(1)) register_1 (.D(wd), .en(decoder_1_out0), .clk(clk), .Q(register_1_q));  // open: clr
  Register #(.width(1)) register_2 (.D(wd), .en(decoder_1_out1), .clk(clk), .Q(register_2_q));  // open: clr
  Register #(.width(1)) register_3 (.D(wd), .en(decoder_1_out2), .clk(clk), .Q(register_3_q));  // open: clr
  Register #(.width(1)) register_4 (.D(wd), .en(decoder_1_out3), .clk(clk), .Q(register_4_q));  // open: clr
  Multiplexer #(.select(2)) multiplexer_1 (
    .in0(register_1_q), .in1(register_2_q), .in2(register_3_q), .in3(register_4_q), .out(read1_out),
    .sel(r1_addr));
  Multiplexer #(.select(2)) multiplexer_2 (
    .in0(register_1_q), .in1(register_2_q), .in2(register_3_q), .in3(register_4_q), .out(read2_out),
    .sel(r2_addr));
endmodule

module write_data (
  input  [3:0] imm,
  input  [7:0] alu_out,
  input  is_li,
  input  is_add,
  output [7:0] w_data
);

  wire [7:0] bit_extender_1_out, multiplexer_1_out;

  assign bit_extender_1_out = {{4{1'b0}}, imm};  // Bit_Extender bit_extender_1
  Multiplexer #(.width(8)) multiplexer_1 (
    .in0({8{1'b0}}), .in1(bit_extender_1_out), .out(multiplexer_1_out), .sel(is_li));
  Multiplexer #(.width(8)) multiplexer_2 (.in0(multiplexer_1_out), .in1(alu_out), .out(w_data), .sel(is_add));
endmodule

module pc_next (
  input  [3:0] pc,
  input  [3:0] addr,
  input  [7:0] r_data1,
  input  [7:0] r_data2,
  input  is_bner0,
  output [3:0] pc_n
);

  wire and_1_out, comparator_1_eq, not_1_out;
  wire [3:0] adder_1_out;

  Comparator comparator_1 (.a(r_data1), .b(r_data2), .eq(comparator_1_eq));  // open: gt, lt
  not not_1 (not_1_out, comparator_1_eq);
  and and_1 (and_1_out, not_1_out, is_bner0);
  Adder #(.width(4)) adder_1 (.a(pc), .b(4'b0001), .out(adder_1_out));  // open: cin, cout
  Multiplexer #(.width(4)) multiplexer_1 (.in0(adder_1_out), .in1(addr), .out(pc_n), .sel(and_1_out));
endmodule

module bin_seg (
  input  D,
  input  in_2,
  input  in_3,
  input  A,
  output g,
  output f,
  output e,
  output out_8,
  output c,
  output b,
  output out_11
);

  wire and_1_out, and_2_out, and_3_out, and_4_out, and_5_out, and_6_out, and_7_out, and_8_out, and_9_out,
       and_10_out, and_11_out, and_12_out, and_13_out, and_14_out, and_15_out, and_16_out, and_17_out,
       and_18_out, and_19_out, and_20_out, and_21_out, and_22_out, and_23_out, and_24_out, and_25_out,
       and_26_out, and_27_out, and_28_out, and_29_out, and_30_out, and_31_out, and_32_out, and_33_out,
       and_34_out, and_35_out, not_1_out, not_2_out, not_3_out, not_4_out;

  not not_1 (not_1_out, D);
  not not_2 (not_2_out, in_2);
  not not_3 (not_3_out, in_3);
  not not_4 (not_4_out, A);
  and and_1 (and_1_out, not_2_out, not_4_out);
  and and_2 (and_2_out, not_1_out, in_3);
  and and_3 (and_3_out, not_1_out, in_2, A);
  and and_4 (and_4_out, D, not_2_out, not_3_out);
  and and_5 (and_5_out, D, not_4_out);
  and and_6 (and_6_out, in_2, in_3);
  and and_7 (and_7_out, not_1_out, not_3_out, not_4_out);
  and and_8 (and_8_out, not_1_out, in_3, A);
  and and_9 (and_9_out, not_2_out, not_4_out);
  and and_10 (and_10_out, D, not_3_out, A);
  and and_11 (and_11_out, not_1_out, not_2_out);
  and and_12 (and_12_out, not_1_out, in_2);
  and and_13 (and_13_out, D, not_2_out);
  and and_14 (and_14_out, not_3_out, A);
  and and_15 (and_15_out, not_2_out, not_3_out);
  and and_16 (and_16_out, not_2_out, A);
  and and_17 (and_17_out, in_2, not_3_out, A);
  and and_18 (and_18_out, not_1_out, not_2_out, not_4_out);
  and and_19 (and_19_out, not_2_out, in_3, A);
  and and_20 (and_20_out, D, not_3_out);
  and and_21 (and_21_out, in_2, in_3, not_4_out);
  and and_22 (and_22_out, not_2_out, not_4_out);
  and and_23 (and_23_out, in_3, not_4_out);
  and and_24 (and_24_out, D, in_3);
  and and_25 (and_25_out, D, in_2);
  and and_26 (and_26_out, not_3_out, not_4_out);
  and and_27 (and_27_out, not_1_out, in_2, not_3_out);
  and and_28 (and_28_out, in_2, not_4_out);
  and and_29 (and_29_out, D, not_2_out);
  and and_30 (and_30_out, D, in_3);
  and and_31 (and_31_out, not_2_out, in_3);
  and and_32 (and_32_out, D, not_2_out);
  and and_33 (and_33_out, not_1_out, in_2, not_3_out);
  and and_34 (and_34_out, in_3, not_4_out);
  and and_35 (and_35_out, D, A);
  or or_1 (g, and_1_out, and_2_out, and_3_out, and_4_out, and_5_out, and_6_out);
  or or_2 (f, and_7_out, and_8_out, and_9_out, and_10_out, and_11_out);
  or or_3 (e, and_12_out, and_13_out, and_14_out, and_15_out, and_16_out);
  or or_4 (out_8, and_17_out, and_18_out, and_19_out, and_20_out, and_21_out);
  or or_5 (c, and_22_out, and_23_out, and_24_out, and_25_out);
  or or_6 (b, and_26_out, and_27_out, and_28_out, and_29_out, and_30_out);
  or or_7 (out_11, and_31_out, and_32_out, and_33_out, and_34_out, and_35_out);
endmodule

module decode_imm (
  input  [31:0] instr,
  output [31:0] immU,
  output [31:0] immI,
  output [31:0] immS
);

  assign immI[31:11] = {{20{instr[31]}}, instr[31]};  // Bit_Extender bit_extender_1

  assign immI[10:0] = instr[30:20];
  assign immS = {immI[31:11], instr[30:25], instr[11:7]};
  assign immU = {instr[31:12], {12{1'b0}}};
endmodule
