// Logisim project logisim_sCPU.circ as structural Verilog: 6 circuits, main circuit main
module main (
);

  sCPU_1 scpu_1_1 ();  // open: pc_in, we, clk, imm, rs2, rs1, rd, is_add, opcode, is_li, addr, is_bner0, is_out
  gpr gpr_1 ();  // open: we, write_addr, clk, read_addr1, write_data, read_addr2, read2_out, read1_out
endmodule

module pc (
  input  [3:0] pc_in,
  input  WE,
  input  clk,
  output [3:0] pc_out
);

  Register #(.width(4)) pc (.D(pc_in), .en(WE), .clk(clk), .Q(pc_out));  // open: clr
endmodule

module decode (
  input  in_1,
  input  in_2,
  input  in_3,
  input  in_4,
  input  in_5,
  input  in_6,
  input  in_7,
  input  in_8,
  output [3:0] imm,
  output [1:0] rs2,
  output [1:0] rs1,
  output [1:0] rd,
  output is_add,
  output [1:0] opcode,
  output is_li,
  output [3:0] addr,
  output is_bner0,
  output is_out
);

  wire not_1_out, not_2_out, not_3_out, not_4_out;

  not not_1 (not_1_out, in_7);
  not not_2 (not_2_out, in_8);
  not not_3 (not_3_out, in_7);
  not not_4 (not_4_out, in_8);
  and and_1 (is_add, not_1_out, not_2_out);
  and and_2 (is_li, in_8, not_3_out);
  and and_3 (is_bner0, in_7, in_8);
  and and_4 (is_out, in_7, not_4_out);

  assign addr = {in_6, in_5, in_4, in_3};
  assign imm = {in_4, in_3, in_2, in_1};
  assign opcode = {in_8, in_7};
  assign rd = {in_6, in_5};
  assign rs1 = {in_4, in_3};
  assign rs2 = {in_2, in_1};
endmodule

module sCPU_1 (
  input  [3:0] pc_in,
  input  we,
  input  clk,
  output [3:0] imm,
  output [1:0] rs2,
  output [1:0] rs1,
  output [1:0] rd,
  output is_add,
  output [1:0] opcode,
  output is_li,
  output [3:0] addr,
  output is_bner0,
  output is_out
);

  wire [3:0] pc_1_pc_out;
  wire [7:0] MEM_data;

  ROM #(.addrWidth(4)) MEM (.addr(pc_1_pc_out), .data(MEM_data));
  pc pc_1 (.pc_in(pc_in), .WE(we), .clk(clk), .pc_out(pc_1_pc_out));
  decode decode_1 (
    .in_1(MEM_data[0]), .in_2(MEM_data[1]), .in_3(MEM_data[2]), .in_4(MEM_data[3]), .in_5(MEM_data[4]),
    .in_6(MEM_data[5]), .in_7(MEM_data[6]), .in_8(MEM_data[7]), .imm(imm), .rs2(rs2), .rs1(rs1), .rd(rd),
    .is_add(is_add), .opcode(opcode), .is_li(is_li), .addr(addr), .is_bner0(is_bner0), .is_out(is_out));

  // Notes on the sheet:
  //   contents of MEM (hex, n*v repeats v):
  //   8a 90 a0 b1 17 29 42 d1 df
endmodule

module gpr (
  input  we,
  input  [1:0] write_addr,
  input  clk,
  input  [1:0] read_addr1,
  input  [7:0] write_data,
  input  [1:0] read_addr2,
  output [7:0] read2_out,
  output [7:0] read1_out
);

  gpr_unit gpr_unit_1 (
    .w_en(we), .w_addr(write_addr), .wd(write_data[0]), .clk(clk), .r1_addr(read_addr1),
    .r2_addr(read_addr2), .read2_out(read2_out[0]), .read1_out(read1_out[0]));
  gpr_unit gpr_unit_2 (
    .w_en(we), .w_addr(write_addr), .wd(write_data[1]), .clk(clk), .r1_addr(read_addr1),
    .r2_addr(read_addr2), .read2_out(read2_out[1]), .read1_out(read1_out[1]));
  gpr_unit gpr_unit_3 (
    .w_en(we), .w_addr(write_addr), .wd(write_data[2]), .clk(clk), .r1_addr(read_addr1),
    .r2_addr(read_addr2), .read2_out(read2_out[2]), .read1_out(read1_out[2]));
  gpr_unit gpr_unit_4 (
    .w_en(we), .w_addr(write_addr), .wd(write_data[3]), .clk(clk), .r1_addr(read_addr1),
    .r2_addr(read_addr2), .read2_out(read2_out[3]), .read1_out(read1_out[3]));
  gpr_unit gpr_unit_5 (
    .w_en(we), .w_addr(write_addr), .wd(write_data[4]), .clk(clk), .r1_addr(read_addr1),
    .r2_addr(read_addr2), .read2_out(read2_out[4]), .read1_out(read1_out[4]));
  gpr_unit gpr_unit_6 (
    .w_en(we), .w_addr(write_addr), .wd(write_data[5]), .clk(clk), .r1_addr(read_addr1),
    .r2_addr(read_addr2), .read2_out(read2_out[5]), .read1_out(read1_out[5]));
  gpr_unit gpr_unit_7 (
    .w_en(we), .w_addr(write_addr), .wd(write_data[6]), .clk(clk), .r1_addr(read_addr1),
    .r2_addr(read_addr2), .read2_out(read2_out[6]), .read1_out(read1_out[6]));
  gpr_unit gpr_unit_8 (
    .w_en(we), .w_addr(write_addr), .wd(write_data[7]), .clk(clk), .r1_addr(read_addr1),
    .r2_addr(read_addr2), .read2_out(read2_out[7]), .read1_out(read1_out[7]));
endmodule

module gpr_unit (
  input  w_en,
  input  [1:0] w_addr,
  input  wd,
  input  clk,
  input  [1:0] r1_addr,
  input  [1:0] r2_addr,
  output read2_out,
  output read1_out
);

  wire decoder_1_out0, decoder_1_out1, decoder_1_out2, decoder_1_out3, register_1_q, register_2_q,
       register_3_q, register_4_q;

  Decoder #(.select(2)) decoder_1 (
    .out0(decoder_1_out0), .out1(decoder_1_out1), .out2(decoder_1_out2), .out3(decoder_1_out3), .sel(w_addr),
    .en(w_en));
  Register #(.width(1)) register_1 (.D(wd), .en(decoder_1_out0), .clk(clk), .Q(register_1_q));  // open: clr
  Register #(.width(1)) register_2 (.D(wd), .en(decoder_1_out1), .clk(clk), .Q(register_2_q));  // open: clr
  Register #(.width(1)) register_3 (.D(wd), .en(decoder_1_out2), .clk(clk), .Q(register_3_q));  // open: clr
  Register #(.width(1)) register_4 (.D(wd), .en(decoder_1_out3), .clk(clk), .Q(register_4_q));  // open: clr
  Multiplexer #(.select(2)) multiplexer_1 (
    .in0(register_1_q), .in1(register_2_q), .in2(register_3_q), .in3(register_4_q), .out(read1_out),
    .sel(r1_addr));
  Multiplexer #(.select(2)) multiplexer_2 (
    .in0(register_1_q), .in1(register_2_q), .in2(register_3_q), .in3(register_4_q), .out(read2_out),
    .sel(r2_addr));
endmodule
